# Fritzing sketch resapirator electronics (saved by Fritzing 0.9.4)

parts:
  Componente1 = Arduino Nano (Rev3.0)
  Componente2 = EasyDriver_v44
  J1 = Power Jack [package=power_jack_combo]
  M1 = Stepper Motor - Bipolar

nets:
  N1: Componente1.D8, Componente2.DIR
  N2: Componente1.D9, Componente2.STEP
  GND: Componente1.GND, Componente2.GND, J1.GND
  N3: Componente2.V+, J1.GNDBREAK
  N4: Componente2.OUT2A, M1.A
  N5: Componente2.OUT2B, M1.C
  N6: Componente2.OUT1A, M1.B
  N7: Componente2.OUT1B, M1.D
